// Logisim project alu.circ as structural Verilog: 1 circuit, main circuit main
module main (
  input  A3,
  input  B3,
  input  A2,
  input  B2,
  input  A1,
  input  B1,
  input  A0,
  input  B0,
  input  c2,
  input  c1,
  input  c0,
  output X3,
  output Y3,
  output C,
  output s3,
  output s2,
  output s1,
  output s0,
  output Z,
  output S,
  output V,
  output X0,
  output Y1,
  output Y0,
  output Z0,
  output X2,
  output X1,
  output Y2,
  output Cout1
);

  wire n7404_1_p2, n7404_1_p3, n7404_1_p4, n7404_1_p6, n7404_1_p7, n7404_1_p8, n7404_1_p9, n7404_2_p3,
       n7408_1_p5, n7408_2_p4, n7408_2_p8, n7408_2_p10, n7408_2_p11, n7408_3_p6, n7432_1_p4, n7432_1_p5,
       n7432_1_p8, n7432_1_p12, n7432_2_p1, n7432_2_p7, n7432_2_p11, n7432_2_p14, n7483_1_p10, n7483_2_p1,
       n7486_1_p11;

  // _7404 7404_1: pin names not known; wires that end beside it: A0, n7404_1_p2, n7404_1_p3, n7404_1_p4, c2, n7404_1_p6, n7404_1_p7, n7404_1_p8, n7404_1_p9
  // _7432 7432_1: pin names not known; wires that end beside it: A0, n7404_1_p2, c0, n7432_1_p4, n7432_1_p5, n7432_1_p5, B0, n7432_1_p8, n7432_1_p4, n7432_1_p5, B1, n7432_1_p12
  // _7486 7486_1: pin names not known; wires that end beside it: B0, c2, n7404_1_p6, B1, c2, c2, B2, n7404_1_p3, c2, B3, n7486_1_p11
  // _7408 7408_1: pin names not known; wires that end beside it: n7432_1_p8, A0, X0, n7432_1_p4, n7408_1_p5, Z0, n7404_1_p8, n7404_1_p7, c0, Y0, n7432_1_p12, A1, X1, A2, X2
  // _7408 7408_2: pin names not known; wires that end beside it: n7404_1_p9, c0, Y1, n7408_2_p4, n7404_1_p4, c0, Y2, n7408_2_p8, n7432_1_p4, n7408_2_p10, n7408_2_p11
  // _7408 7408_3: pin names not known; wires that end beside it: n7408_2_p11, A3, X3, n7432_1_p4, c1, n7408_3_p6, c0, Y3, n7432_1_p4
  // _7432 7432_2: pin names not known; wires that end beside it: n7432_2_p1, n7432_1_p5, B2, n7408_2_p4, n7432_1_p5, B3, n7432_2_p7, C, S, s2, n7432_2_p11, n7432_2_p11, s1, n7432_2_p14
  // _7404 7404_2: pin names not known; wires that end beside it: n7486_1_p11, n7408_3_p6, n7404_2_p3, Z
  // _7483 7483_1: pin names not known; wires that end beside it: X3, n7408_2_p10, n7408_2_p10, n7408_2_p8, 1'b0, 1'b0, Y3, S, n7432_2_p7, n7483_1_p10, Y2, X2, s2
  // _7483 7483_2: pin names not known; wires that end beside it: n7483_2_p1, Y1, n7483_2_p1, Z0, Z0, n7408_1_p5, 1'b0, 1'b0, X1, s1, Cout1, n7432_2_p1, Y0, X0, s0
  // _7486 7486_2: pin names not known; wires that end beside it: C, n7408_2_p8, V
  // _7432 7432_3: pin names not known; wires that end beside it: n7432_2_p14, s0, n7404_2_p3
  // _7408 7408_4: pin names not known; wires that end beside it: n7432_1_p4, Cout1, n7483_1_p10

  assign s3 = S;
endmodule
