// Logisim project ALU.circ as structural Verilog: 10 circuits, main circuit ALU
module ALU (
  input  [7:0] Input1,
  input  [7:0] Input2,
  input  [2:0] AluOp,
  output [7:0] Output,
  output Overflow,
  output Zero
);

  wire Adder_overflow, Substractor_overflow;
  wire [7:0] Adder_result, AND_result, OR_result, SLL_out_3, SRL_out_3, Substractor_result, XOR_result;

  Add Adder (.Input1(Input1), .Input2(Input2), .Result(Adder_result), .Overflow(Adder_overflow));  // open: CarryOut
  Sub Substractor (
    .in_1(Input1), .in_2(Input2), .Result(Substractor_result), .Overflow(Substractor_overflow), .Zero(Zero));
  AND AND (.Input1(Input1), .Input2(Input2), .Result(AND_result));
  OR OR (.Input1(Input1), .Input2(Input2), .Result(OR_result));
  XOR XOR (.Input1(Input1), .Input2(Input2), .Result(XOR_result));
  SLL SLL (.in_1(Input1), .in_2(Input2), .out_3(SLL_out_3));
  SRL SRL (.in_1(Input1), .in_2(Input2), .out_3(SRL_out_3));
  Multiplexer #(.select(3), .width(8)) multiplexer_1 (
    .in0(Adder_result), .in1(Substractor_result), .in2(AND_result), .in3(OR_result), .in4(XOR_result),
    .in5(SLL_out_3), .in7(SRL_out_3), .out(Output), .sel(AluOp));  // open: in6, en
  Multiplexer #(.select(3)) multiplexer_2 (
    .in0(Adder_overflow), .in1(Substractor_overflow), .in2(1'b0), .in3(1'b0), .in4(1'b0), .in5(1'b0),
    .in6(1'b0), .in7(1'b0), .out(Overflow), .sel(AluOp));  // open: en
endmodule

module Add (
  input  [7:0] Input1,
  input  [7:0] Input2,
  output [7:0] Result,
  output Overflow,
  output CarryOut
);

  wire adder_1_cout;

  Adder #(.width(7)) adder_1 (.a(Input1[6:0]), .b(Input2[6:0]), .out(Result[6:0]), .cout(adder_1_cout));  // open: cin
  Adder #(.width(1)) adder_2 (.a(Input1[7]), .b(Input2[7]), .out(Result[7]), .cin(adder_1_cout), .cout(CarryOut));
  // _7486 7486_1: pin names not known; wires that end beside it: adder_1_cout, CarryOut, Overflow
endmodule

module _8_Bit_NOR (
  input  [7:0] in_1,
  output out_2
);

  wire n7432_1_p3, n7432_1_p6, n7432_1_p8, n7432_1_p9, n7432_2_p3, n7432_2_p6, n7432_2_p9;

  // _7432 7432_1: pin names not known; wires that end beside it: in_1[0], in_1[1], n7432_1_p3, n7432_1_p3, in_1[2], n7432_1_p6, in_1[4], n7432_1_p8, n7432_1_p9, in_1[3], n7432_1_p6, n7432_1_p8
  // _7432 7432_2: pin names not known; wires that end beside it: n7432_1_p9, in_1[5], n7432_2_p3, n7432_2_p3, in_1[6], n7432_2_p6, in_1[7], n7432_2_p6, n7432_2_p9
  // _7404 7404_1: pin names not known; wires that end beside it: n7432_2_p9, out_2
endmodule

module Sub (
  input  [7:0] in_1,
  input  [7:0] in_2,
  output [7:0] Result,
  output Overflow,
  output Zero
);

  wire [7:0] negator_1_out;

  Negator negator_1 (.in(in_2), .out(negator_1_out));
  Add add_1 (.Input1(in_1), .Input2(negator_1_out), .Result(Result), .Overflow(Overflow));  // open: CarryOut
  _8_Bit_NOR _8_Bit_NOR (.in_1(Result), .out_2(Zero));
endmodule

module AND (
  input  [7:0] Input1,
  input  [7:0] Input2,
  output [7:0] Result
);

  // _7408 7408_1: pin names not known; wires that end beside it: Input1[0], Input2[0], Result[0], Input1[1], Input2[1], Result[1], Input1[2], Input2[2], Result[2], Input1[3], Input2[3]
  // _7408 7408_2: pin names not known; wires that end beside it: Input1[4], Input2[4], Result[4], Input1[5], Input2[5], Result[5], Result[3], Input1[6], Input2[6], Result[6], Input2[7], Input1[7], Result[7]
endmodule

module OR (
  input  [7:0] Input1,
  input  [7:0] Input2,
  output [7:0] Result
);

  // _7432 7432_1: pin names not known; wires that end beside it: Input1[0], Input2[0], Result[0], Input1[1], Input2[1], Result[1], Input1[2], Input2[2], Result[2], Input1[3], Input2[3]
  // _7432 7432_2: pin names not known; wires that end beside it: Input1[4], Input2[4], Result[4], Input1[5], Input2[5], Result[5], Result[3], Input1[6], Input2[6], Result[6], Input2[7], Input1[7], Result[7]
endmodule

module NOT (
  input  [7:0] in_1,
  output [7:0] out_2
);

  // _7404 7404_1: pin names not known; wires that end beside it: in_1[0], out_2[0], in_1[1], out_2[1], in_1[3], out_2[3], in_1[4]
  // _7404 7404_2: pin names not known; wires that end beside it: in_1[2], out_2[2], in_1[6], out_2[6], in_1[7], out_2[7], out_2[4], in_1[5], out_2[5]
endmodule

module XOR (
  input  [7:0] Input1,
  input  [7:0] Input2,
  output [7:0] Result
);

  // _7486 7486_1: pin names not known; wires that end beside it: Input1[0], Input2[0], Result[0], Input1[1], Input2[1], Result[1], Input1[2], Input2[2], Result[2], Input1[3], Input2[3]
  // _7486 7486_2: pin names not known; wires that end beside it: Input1[4], Input2[4], Result[4], Input1[5], Input2[5], Result[5], Result[3], Input1[6], Input2[6], Result[6], Input2[7], Input1[7], Result[7]
endmodule

module SLL (
  input  [7:0] in_1,
  input  [7:0] in_2,
  output [7:0] out_3
);

  Shifter shifter_1 (.in(in_1), .\dist (in_2[2:0]), .out(out_3));
endmodule

module SRL (
  input  [7:0] in_1,
  input  [7:0] in_2,
  output [7:0] out_3
);

  Shifter #(.shift("lr")) shifter_1 (.in(in_1), .\dist (in_2[2:0]), .out(out_3));
endmodule
