// Logisim project offline3.circ as structural Verilog: 5 circuits, main circuit main
module main (
  input  in_1,
  output [7:0] out_2,
  output [7:0] out_3,
  output [7:0] out_4,
  output [15:0] out_5,
  output [7:0] Result
);

  wire alu_2_zero, clock_1_out, control_1_alusrc, control_1_beq, control_1_branch, control_1_jump,
       control_1_memread, control_1_memtoreg, control_1_memwrite, control_1_regdst, control_1_regwrite,
       n7404_1_p2, n7408_1_p3, n7486_1_p3;
  wire [2:0] control_1_aluop;
  wire [3:0] datamemory_1_read_data, multiplexer_1_out, multiplexer_2_out, multiplexer_4_out,
       multiplexer_4_out_2, registerfile_1_readdata1, registerfile_1_readdata2;
  wire [7:0] alu_1_output, alu_3_output, bit_extender_3_out, bit_extender_4_out, multiplexer_3_out,
       multiplexer_5_out;

  Register register_1 (.D(multiplexer_5_out), .Q(out_4), .clk(clock_1_out), .clr(in_1));  // open: en
  ALU alu_1 (.Input1(out_4), .Input2(8'h1), .AluOp(3'b000), .Output(alu_1_output));  // open: Overflow, Zero
  Instruction_Memory instruction_memory_1 (.Address(out_4), .Output(out_5));
  Clock clock_1 (.out(clock_1_out));
  Multiplexer #(.width(4)) multiplexer_1 (
    .in0(out_5[7:4]), .in1(out_5[3:0]), .out(multiplexer_1_out), .sel(control_1_regdst));  // open: en
  Control control_1 (
    .Opcode(out_5[15:12]), .RegDst(control_1_regdst), .Branch(control_1_branch), .MemRead(control_1_memread),
    .MemToReg(control_1_memtoreg), .ALUOp(control_1_aluop), .MemWrite(control_1_memwrite),
    .ALUSrc(control_1_alusrc), .RegWrite(control_1_regwrite), .beq(control_1_beq), .jump(control_1_jump));
  RegisterFile registerfile_1 (
    .RegWrite(control_1_regwrite), .ReadRegister1(out_5[11:8]), .ReadRegister2(out_5[7:4]),
    .WriteRegister(multiplexer_1_out), .WriteData(multiplexer_4_out), .Clk(clock_1_out),
    .ReadData1(registerfile_1_readdata1), .ReadData2(registerfile_1_readdata2), .Clr(in_1));
  Multiplexer #(.width(4)) multiplexer_2 (
    .in0(registerfile_1_readdata2), .in1(out_5[3:0]), .out(multiplexer_2_out), .sel(control_1_alusrc));  // open: en
  assign out_2 = {{4{1'b0}}, registerfile_1_readdata1};  // Bit_Extender bit_extender_1
  assign out_3 = {{4{1'b0}}, multiplexer_2_out};  // Bit_Extender bit_extender_2
  assign bit_extender_3_out = {{4{1'b0}}, out_5[3:0]};  // Bit_Extender bit_extender_3
  ALU alu_2 (
    .Input1(out_2), .Input2(out_3), .AluOp(control_1_aluop), .Output(Result), .Zero(alu_2_zero));  // open: Overflow
  ALU alu_3 (
    .Input1(alu_1_output), .Input2(bit_extender_3_out), .AluOp(3'b000), .Output(alu_3_output));  // open: Overflow, Zero
  DataMemory datamemory_1 (
    .Address(Result), .Write_Data(registerfile_1_readdata2), .Clock(clock_1_out),
    .MemWrite(control_1_memwrite), .MemRead(control_1_memread), .Read_Data(datamemory_1_read_data));
  assign bit_extender_4_out = {{4{1'b0}}, datamemory_1_read_data};  // Bit_Extender bit_extender_4
  Multiplexer #(.width(8)) multiplexer_3 (
    .in0(alu_1_output), .in1(alu_3_output), .out(multiplexer_3_out), .sel(n7408_1_p3));  // open: en
  // _7486 7486_1: pin names not known; wires that end beside it: control_1_beq, alu_2_zero, n7486_1_p3
  Multiplexer #(.width(8)) multiplexer_4 (
    .in0(Result), .in1(bit_extender_4_out), .out({multiplexer_4_out_2, multiplexer_4_out}),
    .sel(control_1_memtoreg));  // open: en
  Multiplexer #(.width(8)) multiplexer_5 (
    .in0(multiplexer_3_out), .in1(out_5[11:4]), .out(multiplexer_5_out), .sel(control_1_jump));  // open: en
  // _7404 7404_1: pin names not known; wires that end beside it: n7486_1_p3, n7404_1_p2
  // _7408 7408_1: pin names not known; wires that end beside it: n7404_1_p2, control_1_branch, n7408_1_p3
endmodule

module RegisterFile (
  input  RegWrite,
  input  [3:0] ReadRegister1,
  input  [3:0] ReadRegister2,
  input  [3:0] WriteRegister,
  input  [3:0] WriteData,
  input  Clr,
  input  Clk,
  output [3:0] ReadData1,
  output [3:0] ReadData2
);

  wire decoder_1_out0, decoder_1_out1, decoder_1_out2, decoder_1_out3, decoder_1_out4, decoder_1_out7,
       n7408_1_p3, n7408_1_p6, n7408_1_p9, n7408_1_p12, n7408_2_p3, n7408_2_p6;
  wire [3:0] multiplexer_1_out, multiplexer_4_out, t0_q, t1_q, t2_q, t3_q, t4_q, zero_q;

  Decoder #(.select(3)) decoder_1 (
    .out0(decoder_1_out0), .out1(decoder_1_out1), .out2(decoder_1_out2), .out3(decoder_1_out3),
    .out4(decoder_1_out4), .out7(decoder_1_out7), .sel(WriteRegister[2:0]));  // open: out5, out6, en
  Register #(.width(4)) t0 (.D(WriteData), .en(n7408_1_p3), .Q(t0_q), .clk(Clk), .clr(Clr));
  Register #(.width(4)) t1 (.D(WriteData), .en(n7408_1_p6), .Q(t1_q), .clk(Clk), .clr(Clr));
  Register #(.width(4)) t2 (.D(WriteData), .en(n7408_1_p9), .Q(t2_q), .clk(Clk), .clr(Clr));
  Register #(.width(4)) t3 (.D(WriteData), .en(n7408_1_p12), .Q(t3_q), .clk(Clk), .clr(Clr));
  Register #(.width(4)) t4 (.D(WriteData), .en(n7408_2_p3), .Q(t4_q), .clk(Clk), .clr(Clr));
  Register #(.width(4)) zero (.D(4'b0000), .en(n7408_2_p6), .Q(zero_q), .clk(Clk), .clr(Clr));
  // _7408 7408_1: pin names not known; wires that end beside it: decoder_1_out0, RegWrite, n7408_1_p3, decoder_1_out1, RegWrite, n7408_1_p6, decoder_1_out2, RegWrite, n7408_1_p9, decoder_1_out3, RegWrite, n7408_1_p12
  // _7408 7408_2: pin names not known; wires that end beside it: decoder_1_out4, RegWrite, n7408_2_p3, decoder_1_out7, RegWrite, n7408_2_p6
  Multiplexer #(.select(3), .width(4)) multiplexer_1 (
    .in0(t0_q), .in1(t1_q), .in2(t2_q), .in3(t3_q), .in4(t4_q), .in7(zero_q), .out(multiplexer_1_out),
    .sel(ReadRegister1[2:0]));  // open: in5, in6, en
  Multiplexer #(.width(4)) multiplexer_2 (
    .in0(ReadRegister1), .in1(multiplexer_1_out), .out(ReadData1), .sel(ReadRegister1[3]));  // open: en
  Multiplexer #(.width(4)) multiplexer_3 (
    .in0(ReadRegister2), .in1(multiplexer_4_out), .out(ReadData2), .sel(ReadRegister2[3]));  // open: en
  Multiplexer #(.select(3), .width(4)) multiplexer_4 (
    .in0(t0_q), .in1(t1_q), .in2(t2_q), .in3(t3_q), .in4(t4_q), .in7(zero_q), .out(multiplexer_4_out),
    .sel(ReadRegister2[2:0]));  // open: in5, in6, en
endmodule

module DataMemory (
  input  [7:0] Address,
  input  [3:0] Write_Data,
  input  Clock,
  input  MemWrite,
  input  MemRead,
  output [3:0] Read_Data
);

  RAM #(.dataWidth(4), .bus("separate")) ram_1 (
    .addr(Address), .din(Write_Data), .data(Read_Data), .str(MemWrite), .clk(Clock), .ld(MemRead));  // open: sel, clr
endmodule

module Instruction_Memory (
  input  [7:0] Address,
  output [15:0] Output
);

  ROM #(.dataWidth(16)) rom_1 (.addr(Address), .data(Output));  // open: sel

  // Notes on the sheet:
  //   contents of rom_1 (hex, n*v repeats v):
  //   1ff9 1ff9 1ffa b929 ba3a 1a9b
endmodule

module Control (
  input  [3:0] Opcode,
  output RegDst,
  output Branch,
  output MemRead,
  output MemToReg,
  output [2:0] ALUOp,
  output MemWrite,
  output ALUSrc,
  output RegWrite,
  output beq,
  output jump
);

  ROM #(.addrWidth(4), .dataWidth(12)) rom_1 (
    .addr(Opcode), .data({jump, beq, RegWrite, ALUSrc, MemWrite, ALUOp, MemToReg, MemRead, Branch, RegDst}));  // open: sel

  // Notes on the sheet:
  //   contents of rom_1 (hex, n*v repeats v):
  //   231 201 211 12 412 180 800 210 30c 221 260 201 230 241 220 250
  //   ALU Operations
  //   000 -> add
  //   001 -> sub
  //   010 -> and
  //   011 -> or
  //   100 -> nor
  //   101 -> sll
  //   110 -> srl
endmodule
